# Fritzing sketch Task1.1P_Diagram (saved by Fritzing 0.9.3b)
breadboards: 1

parts:
  Arduino_Mega_2560 = Arduino Mega 2560 (Rev3)
  Resistor_1 = Resistor [tolerance=±5% resistance=220 package=THT]
  LED1 = smd LED [color="Red (633nm)" package="1206 [SMD]"]
  Resistor_2 = Resistor [tolerance=±5% resistance=220 package=THT]
  Tilt_Sensor = Tilt Switch [package=THT]

nets:
  N1: Arduino_Mega_2560.GND, Resistor_1.Pin_1, Resistor_2.Pin_1
  N2: Arduino_Mega_2560.D13_PWM, LED1.anode
  N3: Arduino_Mega_2560.5V, Tilt_Sensor.Pin_1
  N4: Arduino_Mega_2560.D2_PWM, Resistor_1.Pin_0, Tilt_Sensor.Pin_2
  N5: LED1.cathode, Resistor_2.Pin_0
