# Fritzing sketch Task1.3C_Diagram (saved by Fritzing 0.9.3b)
breadboards: 1

parts:
  Part1 = Arduino Mega 2560 (Rev3)
  R2 = Resistor [tolerance=±5% resistance=220 package=THT]
  LED1 = smd LED [color="Yellow (595nm)" package="1206 [SMD]"]
  S1 = Tilt Switch [package=THT]
  S2 = Tilt Switch [package=THT]
  R4 = Resistor [tolerance=±5% resistance=220 package=THT]
  R5 = Resistor [tolerance=±5% resistance=220 package=THT]
  LED2 = smd LED [color="Blue (525nm)" package="1206 [SMD]"]
  R6 = Resistor [tolerance=±5% resistance=220 package=THT]

nets:
  N1: Part1.GND, R2.Pin_1, R4.Pin_1, R5.Pin_1, R6.Pin_1
  N2: Part1.D13_PWM, LED1.anode
  N3: Part1.D12_PWM, LED2.anode
  N4: Part1.5V, S1.Pin_1, S2.Pin_1
  N5: Part1.D2_PWM, R2.Pin_0, S1.Pin_2
  N6: Part1.D3_PWM, S2.Pin_2, R4.Pin_0
  N7: LED1.cathode, R5.Pin_0
  N8: LED2.cathode, R6.Pin_0
